# Fritzing sketch internal-addon-board (saved by Fritzing 1.0.6)
circuit board: 4.19999cm x 3.75001cm
breadboards: 1

parts:
  BADGE3 = Hackaday Communicator Badge - main board (back view)
  J1 = female pin header, 2 pins [form="♀ (female)"]
  J2 = female pin header, 2 pins [form="♀ (female)"]
  J3 = female pin header, 2 pins [form="♀ (female)"]
  J4 = female pin header, 2 pins [form="♀ (female)"]
  J5 = female pin header, 2 pins [form="♀ (female)"]
  J6 = female pin header, 2 pins [form="♀ (female)"]

nets:
  N1: BADGE3.J8-1_VCC_(3V3), BADGE3.J6-1_3V3, J2.pin2, J5.pin1, J6.pin1
  N2: BADGE3.J8-2_GND, BADGE3.J6-4_GND
  N3: BADGE3.J8-3_SDA, J4.pin1
  N4: BADGE3.J8-4_SCL, J4.pin2
  N5: BADGE3.J8-5_GPIO1, J3.pin1
  N6: BADGE3.J8-6_GPIO2, J3.pin2
  N7: BADGE3.J6-2_IO11, J1.pin2
  N8: BADGE3.J6-3_IO12, J1.pin1

custom parts:
  Hackaday Communicator Badge - main board (back view): Hackaday Supercon Communicator badge - main board, dimensionally accurate: 148 x 81 mm, generated from the official KiCad design (github.com/Hack-a-Day/2025-Communicator_Badge, MIT license). Exposes the two expansion headers (plain through-holes on the stock badge) as connectors: J8 - SAO v2 port, 2x3, 2.54 mm pitch, hole 1.016 mm: 3V3, GND, SDA (GPIO4), SCL (GPIO5), GPIO1 (GPIO7), GPIO2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
